// Logisim project alu.circ as structural Verilog: 1 circuit, main circuit alu
module alu (
  input  [31:0] A,
  input  [31:0] B,
  input  [3:0] ALUSel,
  output [31:0] ALUResult
);

  wire comparator_1_lt;
  wire [31:0] add0, and_res, mul, mulh, mulhu, or_res, sll0, slt_res, srl_signed, srl_unsigned, sub0, xor_res;

  Adder #(.width(32)) adder_1 (.a(A), .b(B), .out(add0));  // open: cin, cout
  Shifter #(.width(32)) shifter_1 (.in(A), .\dist (B[4:0]), .out(sll0));
  Comparator #(.width(32)) comparator_1 (.a(A), .b(B), .lt(comparator_1_lt));  // open: gt, eq
  assign xor_res = A ^ B;  // XOR_Gate xor_1, 32 bits wide
  Shifter #(.shift("lr"), .width(32)) shifter_2 (.in(A), .\dist (B[4:0]), .out(srl_unsigned));
  assign or_res = A | B;  // OR_Gate or_1, 32 bits wide
  assign and_res = A & B;  // AND_Gate and_1, 32 bits wide
  Multiplier #(.mode("twosComplement"), .width(32)) multiplier_1 (.a(A), .b(B), .out(mul));  // open: cin, cout
  Multiplier #(.mode("twosComplement"), .width(32)) multiplier_2 (.a(A), .b(B), .cout(mulh));  // open: out, cin
  Multiplier #(.width(32)) multiplier_3 (.a(A), .b(B), .cout(mulhu));  // open: out, cin
  Subtractor #(.width(32)) subtractor_1 (.a(A), .b(B), .out(sub0));  // open: bin, bout
  Shifter #(.shift("ar"), .width(32)) shifter_3 (.in(A), .\dist (B[4:0]), .out(srl_signed));
  Multiplexer #(.width(32)) multiplexer_1 (.in0({32{1'b0}}), .in1(32'h1), .out(slt_res), .sel(comparator_1_lt));
  Multiplexer #(.select(4), .width(32)) multiplexer_2 (
    .in0(add0), .in1(sll0), .in2(slt_res), .in4(xor_res), .in5(srl_unsigned), .in6(or_res), .in7(and_res),
    .in8(mul), .in9(mulh), .in11(mulhu), .in12(sub0), .in13(srl_signed), .in15(B), .out(ALUResult),
    .sel(ALUSel));  // open: in3, in10, in14

  // Other names for the same wires on the sheet: bsel[31:0] = B

  // Notes on the sheet:
  //   INPUTS to your circuit
  //   DON'T CHANGE THE LOCATIONS OF THE INPUTS AND OUTPUTS!
  //   OUTPUT from your circuit
endmodule
