// Logisim project control-logic.circ as structural Verilog: 1 circuit, main circuit control_logic
module control_logic (
  input  [31:0] Instruction,
  input  BrEq,
  input  BrLt,
  output PCSel,
  output RegWEn,
  output [2:0] ImmSel,
  output BrUn,
  output ASel,
  output BSel,
  output [3:0] ALUSel,
  output MemWEn,
  output [1:0] WBSel
);

  wire add_0, addi_15, and_1_out, and_2_out, and_3_out, and_4_out, and_11, andi_22, auipc_32, B_type, beq_26,
       bge_29, bgeu_31, blt_28, bltu_30, bne_27, comparator_10_eq, comparator_11_eq, comparator_12_eq,
       comparator_13_eq, comparator_14_eq, comparator_15_eq, comparator_16_eq, comparator_17_eq,
       comparator_18_eq, comparator_19_eq, comparator_20_eq, comparator_21_eq, comparator_22_eq,
       comparator_23_eq, comparator_24_eq, comparator_25_eq, comparator_26_eq, comparator_27_eq,
       comparator_28_eq, comparator_29_eq, comparator_30_eq, comparator_31_eq, comparator_32_eq,
       comparator_33_eq, comparator_34_eq, comparator_35_eq, comparator_36_eq, comparator_37_eq,
       comparator_38_eq, comparator_39_eq, comparator_40_eq, comparator_41_eq, I_type, jal_34, jalr_35,
       L_type, lb_12, lh_13, lui_33, lw_14, mul_1, mulh_4, mulhu_5, not_1_out, not_2_out, not_3_out,
       not_4_out, not_5_out, not_6_out, not_7_out, not_8_out, or_1_out, or_2_out, or_10, ori_21, R_type,
       S_type, sb_23, sh_24, sll_3, slli_16, slt_6, slti_17, sra_9, srai_20, srl_8, srli_19, sub_2, sw_25,
       xor_7, xori_18;
  wire [5:0] InstructionSel;
  wire [15:14] rom_1_data;

  ROM #(.addrWidth(6), .dataWidth(16)) rom_1 (
    .addr(InstructionSel), .data({rom_1_data, WBSel, MemWEn, ALUSel, BSel, ASel, BrUn, ImmSel, RegWEn}));
  Priority_Encoder #(.select_enc(6)) priority_encoder_1 (
    .in0(add_0), .in1(mul_1), .in2(sub_2), .in3(sll_3), .in4(mulh_4), .in5(mulhu_5), .in6(slt_6),
    .in7(xor_7), .in8(srl_8), .in9(sra_9), .in10(or_10), .in11(and_11), .in12(lb_12), .in13(lh_13),
    .in14(lw_14), .in15(addi_15), .in16(slli_16), .in17(slti_17), .in18(xori_18), .in19(srli_19),
    .in20(srai_20), .in21(ori_21), .in22(andi_22), .in23(sb_23), .in24(sh_24), .in25(sw_25), .in26(beq_26),
    .in27(bne_27), .in28(blt_28), .in29(bge_29), .in30(bltu_30), .in31(bgeu_31), .in32(auipc_32),
    .in33(lui_33), .in34(jal_34), .in35(jalr_35), .out(InstructionSel));  // open: in36, in37, in38, in39, in40, in41, in42, in43, in44, in45, in46, in47, in48, in49, in50, in51, in52, in53, in54, in55, in56, in57, in58, in59, in60, in61, in62, in63, gs, en_out, en_in
  Comparator #(.mode("unsigned"), .width(5)) comparator_1 (
    .a(Instruction[6:2]), .b(5'b01100), .eq(R_type));  // open: gt, lt
  Comparator #(.mode("unsigned"), .width(5)) comparator_2 (
    .a(Instruction[6:2]), .b({5{1'b0}}), .eq(L_type));  // open: gt, lt
  Comparator #(.mode("unsigned"), .width(5)) comparator_3 (
    .a(Instruction[6:2]), .b(5'b00100), .eq(I_type));  // open: gt, lt
  Comparator #(.mode("unsigned"), .width(5)) comparator_4 (
    .a(Instruction[6:2]), .b(5'b01000), .eq(S_type));  // open: gt, lt
  Comparator #(.mode("unsigned"), .width(5)) comparator_5 (
    .a(Instruction[6:2]), .b(5'b11000), .eq(B_type));  // open: gt, lt
  Comparator #(.mode("unsigned"), .width(5)) comparator_6 (
    .a(Instruction[6:2]), .b(5'b00101), .eq(auipc_32));  // open: gt, lt
  Comparator #(.mode("unsigned"), .width(5)) comparator_7 (
    .a(Instruction[6:2]), .b(5'b01101), .eq(lui_33));  // open: gt, lt
  Comparator #(.mode("unsigned"), .width(5)) comparator_8 (
    .a(Instruction[6:2]), .b(5'b11011), .eq(jal_34));  // open: gt, lt
  Comparator #(.mode("unsigned"), .width(5)) comparator_9 (
    .a(Instruction[6:2]), .b(5'b11001), .eq(jalr_35));  // open: gt, lt
  Comparator #(.mode("unsigned"), .width(3)) comparator_10 (
    .a(Instruction[14:12]), .b(3'b000), .eq(comparator_10_eq));  // open: gt, lt
  Comparator #(.mode("unsigned"), .width(3)) comparator_11 (
    .a(Instruction[14:12]), .b(3'b000), .eq(comparator_11_eq));  // open: gt, lt
  Comparator #(.mode("unsigned"), .width(3)) comparator_12 (
    .a(Instruction[14:12]), .b(3'b000), .eq(comparator_12_eq));  // open: gt, lt
  Comparator #(.mode("unsigned"), .width(3)) comparator_13 (
    .a(Instruction[14:12]), .b(3'b001), .eq(comparator_13_eq));  // open: gt, lt
  Comparator #(.mode("unsigned"), .width(3)) comparator_14 (
    .a(Instruction[14:12]), .b(3'b001), .eq(comparator_14_eq));  // open: gt, lt
  Comparator #(.mode("unsigned"), .width(3)) comparator_15 (
    .a(Instruction[14:12]), .b(3'b011), .eq(comparator_15_eq));  // open: gt, lt
  Comparator #(.mode("unsigned"), .width(3)) comparator_16 (
    .a(Instruction[14:12]), .b(3'b010), .eq(comparator_16_eq));  // open: gt, lt
  Comparator #(.mode("unsigned"), .width(3)) comparator_17 (
    .a(Instruction[14:12]), .b(3'b100), .eq(comparator_17_eq));  // open: gt, lt
  Comparator #(.mode("unsigned"), .width(3)) comparator_18 (
    .a(Instruction[14:12]), .b(3'b101), .eq(comparator_18_eq));  // open: gt, lt
  Comparator #(.mode("unsigned"), .width(3)) comparator_19 (
    .a(Instruction[14:12]), .b(3'b101), .eq(comparator_19_eq));  // open: gt, lt
  Comparator #(.mode("unsigned"), .width(3)) comparator_20 (
    .a(Instruction[14:12]), .b(3'b110), .eq(comparator_20_eq));  // open: gt, lt
  Comparator #(.mode("unsigned"), .width(3)) comparator_21 (
    .a(Instruction[14:12]), .b(3'b111), .eq(comparator_21_eq));  // open: gt, lt
  or or_1 (or_1_out, bge_29, bgeu_31);
  not not_1 (not_1_out, BrLt);
  not not_2 (not_2_out, BrEq);
  or or_2 (or_2_out, blt_28, bltu_30);
  and and_1 (and_1_out, beq_26, BrEq);
  and and_2 (and_2_out, or_1_out, not_1_out);
  and and_3 (and_3_out, bne_27, not_2_out);
  and and_4 (and_4_out, or_2_out, BrLt);
  not not_3 (not_3_out, Instruction[25]);
  not not_4 (not_4_out, Instruction[30]);
  not not_5 (not_5_out, Instruction[25]);
  not not_6 (not_6_out, Instruction[25]);
  not not_7 (not_7_out, Instruction[30]);
  and and_5 (add_0, R_type, comparator_10_eq, not_3_out, not_4_out);
  and and_6 (mul_1, R_type, comparator_11_eq, Instruction[25]);
  and and_7 (sub_2, R_type, comparator_12_eq, Instruction[30]);
  and and_8 (sll_3, R_type, comparator_13_eq, not_5_out);
  and and_9 (mulh_4, R_type, comparator_14_eq, not_6_out);
  and and_10 (mulhu_5, R_type, comparator_15_eq);
  and u_and_11 (slt_6, R_type, comparator_16_eq);
  and and_12 (xor_7, R_type, comparator_17_eq);
  and and_13 (srl_8, R_type, comparator_18_eq, not_7_out);
  and and_14 (sra_9, R_type, comparator_19_eq, Instruction[30]);
  and and_15 (or_10, R_type, comparator_20_eq);
  and and_16 (and_11, R_type, comparator_21_eq);
  or or_3 (PCSel, and_1_out, and_2_out, and_3_out, and_4_out, jal_34, jalr_35);
  Comparator #(.mode("unsigned"), .width(3)) comparator_22 (
    .a(Instruction[14:12]), .b(3'b000), .eq(comparator_22_eq));  // open: gt, lt
  Comparator #(.mode("unsigned"), .width(3)) comparator_23 (
    .a(Instruction[14:12]), .b(3'b001), .eq(comparator_23_eq));  // open: gt, lt
  Comparator #(.mode("unsigned"), .width(3)) comparator_24 (
    .a(Instruction[14:12]), .b(3'b010), .eq(comparator_24_eq));  // open: gt, lt
  Comparator #(.mode("unsigned"), .width(3)) comparator_25 (
    .a(Instruction[14:12]), .b(3'b000), .eq(comparator_25_eq));  // open: gt, lt
  Comparator #(.mode("unsigned"), .width(3)) comparator_26 (
    .a(Instruction[14:12]), .b(3'b001), .eq(comparator_26_eq));  // open: gt, lt
  Comparator #(.mode("unsigned"), .width(3)) comparator_27 (
    .a(Instruction[14:12]), .b(3'b010), .eq(comparator_27_eq));  // open: gt, lt
  Comparator #(.mode("unsigned"), .width(3)) comparator_28 (
    .a(Instruction[14:12]), .b(3'b100), .eq(comparator_28_eq));  // open: gt, lt
  Comparator #(.mode("unsigned"), .width(3)) comparator_29 (
    .a(Instruction[14:12]), .b(3'b101), .eq(comparator_29_eq));  // open: gt, lt
  Comparator #(.mode("unsigned"), .width(3)) comparator_30 (
    .a(Instruction[14:12]), .b(3'b101), .eq(comparator_30_eq));  // open: gt, lt
  Comparator #(.mode("unsigned"), .width(3)) comparator_31 (
    .a(Instruction[14:12]), .b(3'b110), .eq(comparator_31_eq));  // open: gt, lt
  Comparator #(.mode("unsigned"), .width(3)) comparator_32 (
    .a(Instruction[14:12]), .b(3'b111), .eq(comparator_32_eq));  // open: gt, lt
  not not_8 (not_8_out, Instruction[30]);
  and and_17 (lb_12, L_type, comparator_22_eq);
  and and_18 (lh_13, L_type, comparator_23_eq);
  and and_19 (lw_14, L_type, comparator_24_eq);
  and and_20 (addi_15, I_type, comparator_25_eq);
  and and_21 (slli_16, I_type, comparator_26_eq);
  and and_22 (slti_17, I_type, comparator_27_eq);
  and and_23 (xori_18, I_type, comparator_28_eq);
  and and_24 (ori_21, I_type, comparator_31_eq);
  and and_25 (andi_22, I_type, comparator_32_eq);
  and and_26 (srli_19, I_type, comparator_29_eq, not_8_out);
  and and_27 (srai_20, I_type, comparator_30_eq, Instruction[30]);
  Comparator #(.mode("unsigned"), .width(3)) comparator_33 (
    .a(Instruction[14:12]), .b(3'b000), .eq(comparator_33_eq));  // open: gt, lt
  Comparator #(.mode("unsigned"), .width(3)) comparator_34 (
    .a(Instruction[14:12]), .b(3'b001), .eq(comparator_34_eq));  // open: gt, lt
  Comparator #(.mode("unsigned"), .width(3)) comparator_35 (
    .a(Instruction[14:12]), .b(3'b010), .eq(comparator_35_eq));  // open: gt, lt
  Comparator #(.mode("unsigned"), .width(3)) comparator_36 (
    .a(Instruction[14:12]), .b(3'b000), .eq(comparator_36_eq));  // open: gt, lt
  Comparator #(.mode("unsigned"), .width(3)) comparator_37 (
    .a(Instruction[14:12]), .b(3'b001), .eq(comparator_37_eq));  // open: gt, lt
  Comparator #(.mode("unsigned"), .width(3)) comparator_38 (
    .a(Instruction[14:12]), .b(3'b100), .eq(comparator_38_eq));  // open: gt, lt
  Comparator #(.mode("unsigned"), .width(3)) comparator_39 (
    .a(Instruction[14:12]), .b(3'b101), .eq(comparator_39_eq));  // open: gt, lt
  Comparator #(.mode("unsigned"), .width(3)) comparator_40 (
    .a(Instruction[14:12]), .b(3'b110), .eq(comparator_40_eq));  // open: gt, lt
  Comparator #(.mode("unsigned"), .width(3)) comparator_41 (
    .a(Instruction[14:12]), .b(3'b111), .eq(comparator_41_eq));  // open: gt, lt
  and and_28 (sb_23, S_type, comparator_33_eq);
  and and_29 (sh_24, S_type, comparator_34_eq);
  and and_30 (sw_25, S_type, comparator_35_eq);
  and and_31 (beq_26, B_type, comparator_36_eq);
  and and_32 (bne_27, B_type, comparator_37_eq);
  and and_33 (blt_28, B_type, comparator_38_eq);
  and and_34 (bge_29, B_type, comparator_39_eq);
  and and_35 (bltu_30, B_type, comparator_40_eq);
  and and_36 (bgeu_31, B_type, comparator_41_eq);

  // Other names for the same wires on the sheet: opcode[4:0] = Instruction[6:2]; fun3[2:0] = Instruction[14:12];
  //   func7[6:0] = Instruction[31:25]; Inst25 = Instruction[25]; Inst30 = Instruction[30]

  // Notes on the sheet:
  //   INPUTS to your circuit
  //   contents of rom_1 (hex, n*v repeats v):
  //   1001 1401 1601 1081 1481 1581 1101 1201 1281 1681 1301 1381 41 41 41 1041 10c1 1141 1241 12c1 16c1
  //   1341 13c1 842 842 842 4*64 74 74 1067 17e7 2069 2041
  //   ROM FOR CONTROL LOGIC
  //   DON'T CHANGE THE LOCATIONS OF THE INPUTS AND OUTPUTS!
  //   This is only if you choose to do the ROM option
  //   OUTPUT from your circuit
  //   Reminder: If using ROM, use combinational logic for PCSel
  //   R_type
  //   L_type
  //   I_type
  //   S_type
  //   B_type
endmodule
