// Logisim project cpu.circ as structural Verilog: 1 circuit, main circuit cpu
module cpu (
  input  clk,
  input  [31:0] Instruction,
  input  [31:0] MemReadData,
  output [31:0] MemAddress,
  output [31:0] ProgramCounter,
  output [31:0] ra,
  output [31:0] sp,
  output [31:0] t0,
  output [31:0] t1,
  output [31:0] t2,
  output [31:0] s0,
  output [31:0] s1,
  output [31:0] a0,
  output [3:0] MemWriteMask,
  output [31:0] MemWriteData
);

  wire aSel, brEq, brLt, brUn, bSel, memWEn, pcSel, regWEn;
  wire [1:0] wbSel;
  wire [2:0] immSel;
  wire [3:0] aluSel;
  wire [31:0] adder_1_out, dataToReg, immediate, Instruction_Stage2, multiplexer_1_out, multiplexer_2_out,
       multiplexer_3_out, multiplexer_4_out, PC_add4, ProgramCounter_Stage2, readdata1, readdata2, WB;

  Adder #(.width(32)) adder_1 (.a(ProgramCounter), .b(32'h4), .out(adder_1_out));  // open: cin, cout
  Multiplexer #(.width(32)) multiplexer_1 (.in0(adder_1_out), .in1(MemAddress), .out(multiplexer_1_out), .sel(pcSel));
  Multiplexer #(.width(32)) multiplexer_2 (.in0(Instruction), .in1(32'h13), .out(multiplexer_2_out), .sel(pcSel));
  Register #(.width(32)) PC (.D(multiplexer_1_out), .clk(clk), .Q(ProgramCounter));  // open: en, clr
  Register #(.width(32)) register_1 (.D(multiplexer_2_out), .clk(clk), .Q(Instruction_Stage2));  // open: en, clr
  Register #(.width(32)) register_2 (.D(ProgramCounter), .clk(clk), .Q(ProgramCounter_Stage2));  // open: en, clr
  Adder #(.width(32)) adder_2 (.a(ProgramCounter_Stage2), .b(32'h4), .out(PC_add4));  // open: cin, cout
  control_logic control_logic_1 (
    .Instruction(Instruction_Stage2), .BrEq(brEq), .BrLt(brLt), .PCSel(pcSel), .RegWEn(regWEn),
    .ImmSel(immSel), .BrUn(brUn), .ASel(aSel), .BSel(bSel), .ALUSel(aluSel), .MemWEn(memWEn), .WBSel(wbSel));
  regfile regfile_1 (
    .ReadIndex1(Instruction_Stage2[19:15]), .ReadIndex2(Instruction_Stage2[24:20]),
    .WriteIndex(Instruction_Stage2[11:7]), .WriteData(WB), .RegWEn(regWEn), .clk(clk), .ra(ra), .sp(sp),
    .t0(t0), .t1(t1), .t2(t2), .s0(s0), .s1(s1), .a0(a0), .ReadData1(readdata1), .ReadData2(readdata2));
  imm_gen imm_gen_1 (.Instruction(Instruction_Stage2), .ImmSel(immSel), .Immediate(immediate));
  Multiplexer #(.width(32)) multiplexer_3 (
    .in0(readdata1), .in1(ProgramCounter_Stage2), .out(multiplexer_3_out), .sel(aSel));
  Multiplexer #(.width(32)) multiplexer_4 (.in0(readdata2), .in1(immediate), .out(multiplexer_4_out), .sel(bSel));
  alu alu_1 (.A(multiplexer_3_out), .B(multiplexer_4_out), .ALUSel(aluSel), .ALUResult(MemAddress));
  branch_comp branch_comp_1 (.BrData1(readdata1), .BrData2(readdata2), .BrUn(brUn), .BrEq(brEq), .BrLt(brLt));
  partial_store partial_store_1 (
    .Instruction(Instruction_Stage2), .MemAddress(MemAddress), .DataFromReg(readdata2), .MemWEn(memWEn),
    .MemWriteMask(MemWriteMask), .DataToMem(MemWriteData));
  partial_load partial_load_1 (
    .Instruction(Instruction_Stage2), .MemAddress(MemAddress), .DataFromMem(MemReadData),
    .DataToReg(dataToReg));
  Multiplexer #(.select(2), .width(32)) multiplexer_5 (
    .in0(dataToReg), .in1(MemAddress), .in2(PC_add4), .out(WB), .sel(wbSel));  // open: in3

  // Other names for the same wires on the sheet: aluResult[31:0] = MemAddress; rd[4:0] = Instruction_Stage2[11:7];
  //   rs1[4:0] = Instruction_Stage2[19:15]; rs2[4:0] = Instruction_Stage2[24:20]

  // Notes on the sheet:
  //   To IMEM
  //   IMEM (do **NOT** move this)
  //   From IMEM
  //   Inputs/Outputs for testing. Do **NOT** move these.
  //   To DMEM
  //   DMEM (do **NOT** move this)
  //   From DMEM
endmodule
